# Fritzing sketch Schema (saved by Fritzing 0.9.3b)

parts:
  Part1 = Arduino Uno (Rev3)
  Part2 = KY-019 5V Relay Module [package="Breakout board"]
  LED2 = smd LED [color="Red (633nm)" package="0805 [SMD]"]
  VCC1 = Battery
  R1 = Resistor [tolerance=±5% resistance=220 package="2512 [SMD]"]

nets:
  N1: Part1.D8, Part2.S
  N2: Part1.5V, Part2.+
  N3: Part1.GND, Part2.-
  N4: Part2.Common, R1.Pin_1
  N5: Part2.NO, VCC1.+
  N6: LED2.cathode, VCC1.-
  N7: LED2.anode, R1.Pin_0

custom parts:
  KY-019 5V Relay Module: KY-019 5V Relay module, used to control AC circuits.
